# Fritzing sketch Circuit diagram (saved by Fritzing 0.9.3b)
breadboards: 1

parts:
  S1 = Pushbutton [package="[SMD]"]
  S2 = Pushbutton [package="[SMD]"]
  R1 = Resistor [tolerance=±5% resistance=1k package=THT]
  R2 = Resistor [tolerance=±5% resistance=1k package=THT]
  Part1 = Arduino Nano (Rev3.0) (ICSP)

nets:
  N1: S1.Pin_1, S1.Pin_2, R2.Pin_0
  N2: S1.Pin_3, S1.Pin_4, Part1.D3
  N3: S2.Pin_1, S2.Pin_2, R1.Pin_0
  N4: S2.Pin_3, S2.Pin_4, Part1.D5
  N5: R1.Pin_1, R2.Pin_1, Part1.GND
